# Fritzing sketch design with complex soft latching circuit (saved by Fritzing 0.9.3b)
circuit board: 6.15cm x 5.75025cm
breadboards: 1

parts:
  BATTERY = LIPO-1000mAh [package=lipo-1000]
  IMU = MPU-6050 Board GY-521 [form="♀ (female)" package=THT]
  ON/OFF_Switch = SWITCH-MOMENTARY-2 [package=tactile-pth-12mm]
  D3 = Diode [package=diode-1n4148]
  PRESSURE = Basic Force Sensing Resistor (FSR) [package=THT]
  D4 = Diode [package=diode-1n4148]
  Q3 = Basic FET P-Channel [package="DPak [SMD]"]
  BLUETOOTH = Bluetooth HC-05 Macho
  Q4 = MOSFET-NCHANNEL [package=to220v]
  Part5 = Arduino MKR1000
  R5 = Resistor [tolerance=±5% resistance=10k package=THT]
  R6 = Resistor [tolerance=±5% resistance=10k package=THT]
  R4 = Resistor [tolerance=±5% resistance=10k package=THT]
  Part6 = NRF24L01+ Breakout Board  # not connected

nets:
  N1: BATTERY.+, ON/OFF_Switch.1, D4.C, Q3.drain, R4.Pin_1
  GND: BATTERY.-, IMU.pin2, BLUETOOTH.GND, Q4.D, Part5.GND, R5.Pin_1, R6.Pin_1
  VCC: IMU.pin1, PRESSURE.pin_0, BLUETOOTH.VCC, Part5.VCC
  N2: IMU.pin3, Part5.D12_SCL
  N3: IMU.pin4, Part5.D11_SDA
  N4: ON/OFF_Switch.2, D3.A
  N5: D3.C, D4.A, Q3.source, Part5.AREF
  N6: PRESSURE.pin_1, Part5.A5, R5.Pin_0
  N7: Q3.Gate, Q4.S, R4.Pin_0
  N8: BLUETOOTH.TXD, Part5.D13_RX
  N9: BLUETOOTH.RXD, Part5.14_TX
  N10: Q4.G, Part5.D5_PWM, R6.Pin_0

custom parts:
  MPU-6050 Board GY-521: Acelerometro y Giroscopio MPU-6050 Board GY-521
  Arduino MKR1000: MKR1000 is a powerful board that combines the functionality of the Zero and the Wi-Fi Shield. It is the ideal solution for makers wanting to design IoT projects with minimal previous experience in networking
