# Fritzing sketch design with simple soft latching circuit (saved by Fritzing 0.9.3b)
circuit board: 5cm x 4cm
breadboards: 1

parts:
  D = Diode [package=diode-1n4148]
  P = Basic Force Sensing Resistor (FSR) [package=THT]
  BT = Bluetooth HC-05 Macho
  RF24 = NRF24L01+ Breakout Board
  Q1 = MOSFET-NCHANNEL [package=sot23-3]
  IMU = MPU-9250-half [form=male package=THT]
  R5 = Resistor [tolerance=±5% resistance=10k package="1206 [SMD]"]
  R4 = Resistor [tolerance=±5% resistance=10k package="1206 [SMD]"]
  D_2 = Diode [package=diode-1n4148]
  BZ = Piezo Speaker
  BAT = LIPO-1000mAh with pcb pins [package=lipo-1000]
  Mirza_v0 = BAT Arduino MKR1000
  S1 = SWITCH-MOMENTARY-2 [package=tactile-pth-12mm]

nets:
  N1: D.A, Mirza_v0.D4_PWM, S1.1
  N2: D.C, Q1.S, D_2.A, Mirza_v0.BAT+
  VCC: P.pin_0, BT.VCC, RF24.VCC, IMU.VCC, Mirza_v0.VCC
  N3: P.pin_1, R5.Pin_0, Mirza_v0.A2
  N4: BT.TXD, Mirza_v0.D13_RX
  N5: BT.RXD, Mirza_v0.14_TX
  GND: BT.GND, RF24.GND, IMU.GND, R5.Pin_1, R4.Pin_1, BZ.pin1, BAT.-, Mirza_v0.GND, Mirza_v0.BAT-
  N6: RF24.CE, Mirza_v0.D0
  N7: RF24.CS, Mirza_v0.D1
  N8: RF24.SCK, Mirza_v0.D9_SCK
  N9: RF24.MOSI, Mirza_v0.D8_MOSI
  N10: RF24.MISO, Mirza_v0.D10_MISO
  N11: Q1.G, R4.Pin_0, Mirza_v0.A3
  N12: Q1.D, D_2.C, BAT.+, S1.2
  N13: IMU.SCL, Mirza_v0.D12_SCL
  N14: IMU.SDA, Mirza_v0.D11_SDA
  N15: BZ.pin2, Mirza_v0.A4

custom parts:
  MPU-9250-half: Acelerometro y Giroscopio MPU-9250 Board, extra piece broken to make it half and only using the upper 4 pins. Assumes pins are male (original pins are female)
  LIPO-1000mAh with pcb pins: 1000mAh Lipo-battery with pcb pins
  BAT Arduino MKR1000: MKR1000 is a powerful board that combines the functionality of the Zero and the Wi-Fi Shield. It is the ideal solution for makers wanting to design IoT projects with minimal previous experience in networking
  SWITCH-MOMENTARY-2: Various NO switches- pushbuttons, reed, etc
