# Fritzing sketch razor (saved by Fritzing 0.9.3b)
breadboards: 1

parts:
  Part1 = Arduino MKR1000
  Part2 = Bluetooth HC-05 Macho
  GY1 = MPU-6050 Board GY-521 [form="♀ (female)" package=THT]
  U1 = LIPO-1000mAh [package=lipo-1000]
  J1 = Basic Force Sensing Resistor (FSR) [package=THT]
  R1 = Resistor [tolerance=±5% resistance=10k package=THT]
  U2 = RELAY [package=relay-jzc]
  S1 = Round Pushbutton
  D1 = Schottky Diode [part_number=1N5817 package="Melf DO-213 AB [SMD]"]

nets (from the breadboard view):
  VCC: Part1.VCC, Part2.VCC, GY1.pin1, J1.pin_0
  GND: Part1.GND, Part2.GND, GY1.pin2, R1.Pin_1
  N1: Part1.D11_SDA, GY1.pin4
  N2: Part1.D12_SCL, GY1.pin3
  N3: Part1.D13_RX, Part2.TXD
  N4: Part1.A3, J1.pin_1, R1.Pin_0
  N5: U1.+, U2.NO, U2.MAIN, D1.anode
  N6: U1.-, U2.COIL2
  N7: U2.NC, S1.leg0
  N8: S1.leg1, D1.cathode

custom parts:
  Arduino MKR1000: MKR1000 is a powerful board that combines the functionality of the Zero and the Wi-Fi Shield. It is the ideal solution for makers wanting to design IoT projects with minimal previous experience in networking
  MPU-6050 Board GY-521: Acelerometro y Giroscopio MPU-6050 Board GY-521
